# Fritzing sketch schema (saved by Fritzing 0.9.3b)

parts:
  Raspberry_Pi1 = Raspberry Pi 2
  Composant1 = 16 NeoPixel Ring [part_number=1463]
  Composant2 = 24 NeoPixel Ring [part_number=1586]

nets:
  GND: Raspberry_Pi1.GND, Composant1.GND, Composant2.GND
  N1: Raspberry_Pi1.GPIO12, Composant2.IN
  N2: Raspberry_Pi1.GPIO18, Composant1.IN
  VDD: Raspberry_Pi1.5V, Composant1.VDD, Composant2.VDD

custom parts:
  16 NeoPixel Ring: 16 ultra bright smart LED NeoPixels are arranged in a circle with 1.75" (44.5mm) outer diameter. The rings are 'chainable' - connect the output pin of one to the input pin of another. Use only one microcontroller pin to control as many as you can chain together! Each LED is addressable as the driver chip is inside the LED. Each one has ~18mA constant current drive so the color will be very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
  24 NeoPixel Ring: 24 ultra bright smart LED NeoPixels are arranged in a circle with 2.6" (66mm) outer diameter. The rings are 'chainable' - connect the output pin of one to the input pin of another. Use only one microcontroller pin to control as many as you can chain together! Each LED is addressable as the driver chip is inside the LED. Each one has ~18mA constant current drive so the color will be very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
